# Fritzing sketch bc-coffe (saved by Fritzing 0.9.3b)

parts:
  S1 = Round Pushbutton
  S2 = Round Pushbutton
  R1 = Resistor [tolerance=±5% resistance=220 package="2512 [SMD]"]
  R3 = Resistor [tolerance=±5% resistance=220 package="2512 [SMD]"]
  LED1 = RGB LED - (4 legs) [package="5 mm [THT]"]
  U2 = ESP8266 NodeMCU LoLin module

nets:
  N1: S1.leg0, R1.Pin_0, U2.D1
  N2: S1.leg1, S2.leg0, U2.3V3
  N3: S2.leg1, R3.Pin_0, U2.D2
  N4: R1.Pin_1, R3.Pin_1, LED1.common_anode, U2.GND
  N5: LED1.green_cathode, U2.D3
  N6: LED1.blue_cathode, U2.D4

custom parts:
  ESP8266 NodeMCU LoLin module: ESP8266 based NodeMCU
